# Fritzing sketch AudioMessage (saved by Fritzing 0.9.10b)
breadboards: 2

parts:
  DFRobot_DFPlayer_Mini1 = DFRobot DFPlayer Mini [part_number=DFR0299]
  U1 = ESP32-38PinWide [part_number=ESP32-38PinWide]
  AMP1 = GF1002 Stereo Amplifier
  S1 = Pushbutton [package="[THT]"]
  S2 = Pushbutton [package="[THT]"]
  S3 = Pushbutton [package="[THT]"]
  R1 = Resistor [tolerance=±5% power=0.25 resistance=220 package=THT]
  R2 = Resistor [tolerance=±5% power=0.25 resistance=220 package=THT]
  R3 = Resistor [tolerance=±5% power=0.25 resistance=220 package=THT]
  R4 = Resistor [tolerance=±5% power=0.25 resistance=220 package=THT]
  SP1 = SPEAKER [package=pcb_mount_speaker]

nets:
  VCC: DFRobot_DFPlayer_Mini1.VCC, DFRobot_DFPlayer_Mini1.TX, U1.VIN, U1.GPIO16, AMP1.POWER+, R4.Pin_1
  N1: DFRobot_DFPlayer_Mini1.DAC_R, AMP1.INPUTR
  N2: DFRobot_DFPlayer_Mini1.DAC_L, AMP1.INPUTL
  N3: DFRobot_DFPlayer_Mini1.GND-1, DFRobot_DFPlayer_Mini1.GND-2, U1.GND, AMP1.POWER-, AMP1.INPUTG, R4.Pin_0
  N4: U1.3.3, R1.Pin_1, R2.Pin_1, R3.Pin_1
  N5: U1.GPIO34, S3.Pin_1, S3.Pin_2, R1.Pin_0
  N6: U1.GPIO33, S1.Pin_1, S1.Pin_2, R2.Pin_0
  N7: U1.GPIO14, S2.Pin_1, S2.Pin_2, R3.Pin_0
  N8: U1.GPIO11, S1.Pin_3, S1.Pin_4, S2.Pin_3, S2.Pin_4, S3.Pin_3, S3.Pin_4
  N9: AMP1.LOUT+, SP1.-
  N10: AMP1.LOUT-, SP1.+

notes:
  R = 10k ohms

custom parts:
  ESP32-38PinWide: Generic 38-Pin ESP32 with wide format (only access to one side of pins on a breadboard) based on Stephen Lilley's HiLetgo ESP-WROOM-32 ESP32 ESP-32S Development Board.
  GF1002 Stereo Amplifier: GF1002 6 Watt Stereo Amplifier
